# Fritzing sketch camera (saved by Fritzing 0.9.3b)
breadboards: 1

parts:
  Part1 = Photon  # not connected
  J1 = VC0706 Camera [form="♀ (female)" package=THT]
  Part2 = Photon

nets:
  N1: J1.TX, Part2.D2
  N2: J1.RX, Part2.D3
  GND: J1.GND, Part2.GND
  5V: J1.5V, Part2.VIN

custom parts:
  VC0706 Camera: Generic female header
